# Fritzing sketch waterAlarmSensor (saved by Fritzing 0.9.3b)
breadboards: 1

parts:
  U1 = LuaNode32 / ESP32
  J1 = Piezo Speaker
  R2 = Resistor [tolerance=±5% resistance=220 package=THT]
  R3 = Resistor [tolerance=±5% resistance=220 package=THT]
  LED1 = LED - 5mm [color="Green (555nm)" package="5 mm [THT]"]
  LED2 = LED - 5mm [color="Red (633nm)" package="5 mm [THT]"]
  LED3 = smd LED [color="Blue (430nm)" package="0805 [SMD]"]
  R4 = Resistor [tolerance=±5% resistance=220 package=THT]
  PP_Float_Switch = Round Pushbutton

nets:
  N1: U1.D27, J1.pin1, LED1.cathode, LED2.cathode, LED3.cathode, PP_Float_Switch.leg0, PP_Float_Switch.leg1
  N2: U1.D13, J1.pin2
  N3: U1.RX2, R2.Pin_1
  N4: U1.TX2, R3.Pin_1
  N5: U1.D19, R4.Pin_1
  N6: R2.Pin_0, LED2.anode
  N7: R3.Pin_0, LED3.anode
  N8: LED1.anode, R4.Pin_0

custom parts:
  LuaNode32 / ESP32: ESP32 based LuaNode32
